// Logisim project seven_segment_indicator.circ as structural Verilog: 1 circuit, main circuit main
module main (
  input  in_1,
  input  in_2,
  input  in_3,
  input  in_4
);

  wire a_out, and_1_out, and_2_out, and_3_out, and_4_out, and_5_out, and_6_out, and_7_out, and_8_out,
       and_9_out, and_10_out, and_11_out, and_12_out, and_13_out, and_14_out, and_15_out, and_16_out, b_out,
       c_out, d_out, e_out, f_out, not_1_out, not_2_out, not_3_out, not_4_out, or_1_out, or_2_out, or_3_out,
       or_4_out, or_5_out, or_6_out, or_7_out, or_8_out, or_9_out, or_10_out, or_11_out, or_12_out,
       or_13_out, or_14_out, or_15_out, or_16_out, or_17_out, or_18_out, or_19_out, or_20_out, or_21_out,
       or_22_out, or_23_out, or_24_out, or_25_out, or_26_out, or_27_out, or_28_out, or_29_out, or_30_out,
       or_31_out, or_32_out, or_33_out, or_34_out, or_35_out, or_36_out, or_37_out, or_38_out, or_39_out,
       or_40_out, or_41_out, or_42_out, or_43_out, or_44_out, or_45_out, or_46_out, or_47_out,
       shift_register_1_p5, shift_register_1_p6, shift_register_1_p7, shift_register_1_p8;

  // Shift_Register shift_register_1: pin names not known; wires that end beside it: in_1, in_3, in_4, in_2, shift_register_1_p5, shift_register_1_p6, shift_register_1_p7, shift_register_1_p8
  not not_1 (not_1_out, shift_register_1_p8);
  not not_2 (not_2_out, shift_register_1_p7);
  not not_3 (not_3_out, shift_register_1_p6);
  not not_4 (not_4_out, shift_register_1_p5);
  or or_1 (or_1_out, shift_register_1_p8, shift_register_1_p7);
  or or_2 (or_2_out, shift_register_1_p6, not_4_out);
  or or_3 (or_3_out, shift_register_1_p8, not_2_out);
  or or_4 (or_4_out, shift_register_1_p6, shift_register_1_p5);
  or or_5 (or_5_out, shift_register_1_p8, not_2_out);
  or or_6 (or_6_out, shift_register_1_p6, not_4_out);
  or or_7 (or_7_out, shift_register_1_p8, not_2_out);
  or or_8 (or_8_out, not_3_out, shift_register_1_p5);
  or or_9 (or_9_out, shift_register_1_p8, shift_register_1_p7);
  or or_10 (or_10_out, not_3_out, shift_register_1_p5);
  or or_11 (or_11_out, shift_register_1_p8, shift_register_1_p7);
  or or_12 (or_12_out, shift_register_1_p6, not_4_out);
  or or_13 (or_13_out, shift_register_1_p8, not_2_out);
  or or_14 (or_14_out, shift_register_1_p6, shift_register_1_p5);
  or or_15 (or_15_out, shift_register_1_p8, not_2_out);
  or or_16 (or_16_out, not_3_out, not_4_out);
  and and_1 (and_1_out, not_1_out, not_2_out);
  and and_2 (and_2_out, not_3_out, not_4_out);
  and and_3 (and_3_out, not_1_out, not_2_out);
  and and_4 (and_4_out, shift_register_1_p6, not_4_out);
  and and_5 (and_5_out, not_1_out, shift_register_1_p7);
  and and_6 (and_6_out, shift_register_1_p6, not_4_out);
  and and_7 (and_7_out, shift_register_1_p8, not_2_out);
  and and_8 (and_8_out, not_3_out, not_4_out);
  or or_17 (or_17_out, shift_register_1_p8, shift_register_1_p7);
  or or_18 (or_18_out, shift_register_1_p6, not_4_out);
  or or_19 (or_19_out, shift_register_1_p8, shift_register_1_p7);
  or or_20 (or_20_out, not_3_out, shift_register_1_p5);
  or or_21 (or_21_out, shift_register_1_p8, shift_register_1_p7);
  or or_22 (or_22_out, not_3_out, not_4_out);
  or or_23 (or_23_out, shift_register_1_p8, not_2_out);
  or or_24 (or_24_out, not_3_out, not_4_out);
  or or_25 (or_25_out, shift_register_1_p8, shift_register_1_p7);
  or or_26 (or_26_out, shift_register_1_p6, shift_register_1_p5);
  or or_27 (or_27_out, shift_register_1_p8, shift_register_1_p7);
  or or_28 (or_28_out, shift_register_1_p6, not_4_out);
  or or_29 (or_29_out, shift_register_1_p8, not_2_out);
  or or_30 (or_30_out, not_3_out, not_4_out);
  or or_31 (or_31_out, or_1_out, or_2_out);
  or or_32 (or_32_out, or_3_out, or_4_out);
  or or_33 (or_33_out, or_5_out, or_6_out);
  or or_34 (or_34_out, or_7_out, or_8_out);
  or or_35 (or_35_out, or_9_out, or_10_out);
  or or_36 (or_36_out, or_11_out, or_12_out);
  or or_37 (or_37_out, or_13_out, or_14_out);
  or or_38 (or_38_out, or_15_out, or_16_out);
  and and_9 (and_9_out, and_1_out, and_2_out);
  and and_10 (and_10_out, and_3_out, and_4_out);
  and and_11 (and_11_out, and_5_out, and_6_out);
  and and_12 (and_12_out, and_7_out, and_8_out);
  or or_39 (or_39_out, or_17_out, or_18_out);
  or or_40 (or_40_out, or_19_out, or_20_out);
  or or_41 (or_41_out, or_21_out, or_22_out);
  or or_42 (or_42_out, or_23_out, or_24_out);
  or or_43 (or_43_out, or_25_out, or_26_out);
  or or_44 (or_44_out, or_27_out, or_28_out);
  or or_45 (or_45_out, or_29_out, or_30_out);
  and a (a_out, or_31_out, or_32_out);
  and b (b_out, or_33_out, or_34_out);
  and and_13 (and_13_out, or_36_out, or_37_out);
  or or_46 (or_46_out, and_9_out, and_10_out);
  or or_47 (or_47_out, and_11_out, and_12_out);
  and and_14 (and_14_out, or_39_out, or_40_out);
  and and_15 (and_15_out, or_41_out, or_42_out);
  and and_16 (and_16_out, or_43_out, or_44_out);
  and c (c_out, and_13_out, or_38_out);
  or d (d_out, or_46_out, or_47_out);
  and e (e_out, and_14_out, and_15_out);
  and f (f_out, and_16_out, or_45_out);
  _7_Segment_Display u_7_segment_display_1 (
    .g(f_out), .f(e_out), .a(a_out), .b(b_out), .e(d_out), .d(c_out), .c(or_35_out));  // open: dp
endmodule
